# Fritzing sketch hardware-serial (saved by Fritzing 0.9.2b)

parts:
  Part1 = Logic Level Converter
  Part2 = MAX3232
  U1 = ESP32S-HiLetgo [part_number=ESP32S-HiLetgo]

nets:
  GND: Part1.GND, Part2.GND, U1.GND
  N1: Part1.LV, U1.3.3
  N2: Part1.RX_LV, U1.GPIO16
  N3: Part1.TX_LV, U1.GPIO17
  N4: Part1.TX_HV, Part2.RXD
  N5: Part1.RX_HV, Part2.TXD
  VCC: Part1.HV, Part2.VCC, U1.5V

notes:
  Important!
  Level Logic Converter Tx and Rx pins swap across the HV LV
  Tx pin is IO17
  Rx pin is IO16
  Then entire system is connected to the USB for power

custom parts:
  MAX3232: A random MAX3232 Breakout Board from AliExpress (RS232-TTL-Converter)
  ESP32S-HiLetgo: HiLetgo ESP-WROOM-32 ESP32 ESP-32S Development Board 2.4GHz Dual-Mode WiFi + Bluetooth Dual Cores Microcontroller The ESP32 integrated with Antenna switches, RF Balun, power amplifiers, low-noise amplifiers, filters, and management modules, and the entire solution occupies the least area of PCB. 2.4 GHz Wi-Fi plus Bluetooth dual-mode chip, with TSMC Ultra-low power consumption 40nm technology,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
